# Fritzing sketch connectionSchema (saved by Fritzing 0.9.3b)
perfboards: 2

parts:
  Arduino_CNC_Shield_V3_00_1 = Arduino_CNC_V3.00
  Part2 = Bluetooth HC-05 Macho
  J2 = male pin header, 6 pins [form="♂ (male)"]
  J3 = male pin header, 6 pins [form="♂ (male)"]
  J4 = male pin header, 6 pins [form="♂ (male)"]
  U1 = RELAY [package=relay-jzc]
  M1 = Stepper Motor - Bipolar
  M2 = Stepper Motor - Bipolar
  M3 = Stepper Motor - Bipolar
  Power_plug1 = Power plug
  J5 = male pin header, 4 pins [form="♂ (male)"]
  J6 = male pin header, 4 pins [form="♂ (male)"]
  J7 = male pin header, 4 pins [form="♂ (male)"]
  J8 = male pin header, 4 pins [form="♂ (male)"]
  S1 = Square Pushbutton
  S2 = Round Pushbutton
  S3 = Square Pushbutton
  S4 = Square Pushbutton
  M4 = DC Motor
  Power_plug2 = Power plug

nets:
  5V: Arduino_CNC_Shield_V3_00_1.5V, Part2.VCC, J2.pin1, J2.pin2, J2.pin3, J2.pin4, J2.pin5, J2.pin6, J3.pin1, J3.pin2, J3.pin3, J3.pin4, J3.pin5, J3.pin6
  N1: Arduino_CNC_Shield_V3_00_1.GND#12, Part2.GND, J4.pin1, J4.pin2, J4.pin3, J4.pin4, J4.pin5, J4.pin6, U1.COIL2, U1.NC
  N2: Arduino_CNC_Shield_V3_00_1.POWER_-, Power_plug1.GND
  N3: Arduino_CNC_Shield_V3_00_1.POWER_+, Power_plug1.VCC
  N4: Arduino_CNC_Shield_V3_00_1.X-MTR_'1', M1.D
  N5: Arduino_CNC_Shield_V3_00_1.X-MTR_'2', M1.B
  N6: Arduino_CNC_Shield_V3_00_1.X-MTR_'3', M1.C
  N7: Arduino_CNC_Shield_V3_00_1.X-MTR_'4', M1.A
  N8: Arduino_CNC_Shield_V3_00_1.Z-MTR_'1', M2.D
  N9: Arduino_CNC_Shield_V3_00_1.Z-MTR_'2', M2.B
  N10: Arduino_CNC_Shield_V3_00_1.Z-MTR_'3', M2.C
  N11: Arduino_CNC_Shield_V3_00_1.Z-MTR_'4', M2.A
  N12: Arduino_CNC_Shield_V3_00_1.Y-MTR_'1', M3.D
  N13: Arduino_CNC_Shield_V3_00_1.Y-MTR_'2', M3.B
  N14: Arduino_CNC_Shield_V3_00_1.Y-MTR_'3', M3.C
  N15: Arduino_CNC_Shield_V3_00_1.Y-MTR_'4', M3.A
  N16: Arduino_CNC_Shield_V3_00_1.RX, Part2.RXD
  N17: Arduino_CNC_Shield_V3_00_1.TX, Part2.TXD
  N18: Arduino_CNC_Shield_V3_00_1.SpnEn_/_Z_Limit, U1.NO
  N19: Arduino_CNC_Shield_V3_00_1.Abort, J6.pin1, J7.pin1, S4.leg1
  N20: Arduino_CNC_Shield_V3_00_1.Abort_(Gnd), J5.pin1, J8.pin1, S4.leg0
  N21: Arduino_CNC_Shield_V3_00_1.Hold, J6.pin2, J7.pin2, S1.leg1
  N22: Arduino_CNC_Shield_V3_00_1.Hold_(Gnd), J5.pin2, J8.pin2, S1.leg0
  N23: Arduino_CNC_Shield_V3_00_1.Resume, J6.pin3, J7.pin3, S3.leg1
  N24: Arduino_CNC_Shield_V3_00_1.Resume_(Gnd), J5.pin3, J8.pin3, S3.leg0
  N25: Arduino_CNC_Shield_V3_00_1.E-STOP, Part2.State, J6.pin4, J7.pin4, S2.leg1
  N26: Arduino_CNC_Shield_V3_00_1.E-STOP_(Gnd), J5.pin4, J8.pin4, S2.leg0
  N27: U1.MAIN, Power_plug2.VCC
  N28: U1.COIL1, M4.pin_1
  N29: M4.pin_2, Power_plug2.GND

notes:
  Probe wire

custom parts:
  Arduino_CNC_V3.00: Protoneer Arduino CNC Shield V3.00 If using Grbl V0.9: The “A” axis can not be used (yet). The “SCL” (Arduino A5) pin is now used for 'Probing' input. The “End Stops Z+ & Z-” (Arduino D11) and “SpnEn” (Arduino D12) have been switched!
