# Fritzing sketch mosfetSchema (saved by Fritzing 0.9.3b)
perfboards: 1

parts:
  Q1 = Basic FET P-Channel [part_number=IRFZ44 package="D2Pak [SMD]"]  # not connected
  J1 = male pin header, 4 pins [form="♂ (male)"]
  R1 = Resistor [tolerance=±5% resistance=220 package=THT]  # not connected
  R2 = Resistor [tolerance=±5% resistance=10k package=THT]
  J2 = male pin header, 4 pins [form="♂ (male)"]
  J3 = male pin header, 4 pins [form="♂ (male)"]  # not connected
  Part1 = Arduino Uno (Rev3)  # not connected
  Power_plug1 = Power plug  # not connected
  LED1 = LED - 5mm [color="Red (633nm)" package="5 mm [THT]"]
  R3 = Resistor [tolerance=±5% resistance=220 package=THT]
  M1 = DC Motor  # not connected

nets:
  N1: J1.pin1, J2.pin1
  N2: J1.pin3, R2.Pin_1
  N3: LED1.anode, R3.Pin_1

notes:
  Condivide GND
  Example pin signal
  Using signal pin to show led indicator
  12v DC power
