# Fritzing sketch noiseRemover (saved by Fritzing 0.9.3b)
perfboards: 1

parts:
  R1 = Resistor [tolerance=±5% resistance=680 package=THT]
  R2 = Resistor [tolerance=±5% resistance=2.2k package=THT]
  C1 = Electrolytic Capacitor [capacitance=47nF package="100 mil [THT, electrolytic]"]
  J1 = male pin header, 2 pins [form="♂ (male)"]
  J2 = male pin header, 3 pins [form="♂ (male)"]

nets:
  N1: R1.Pin_0, R2.Pin_0, J1.pin1
  N2: R1.Pin_1, J2.pin1
  N3: R2.Pin_1, C1.+, J2.pin2
  N4: C1.-, J1.pin2

notes:
  VCC
  Signal
  GND
  Clip touch
  Clip alligator
