# Fritzing sketch spindleSignalToNeg (saved by Fritzing 0.9.3b)
perfboards: 1

parts:
  Q1 = TRANSISTOR_NPN [package=to-92]
  R1 = Resistor [tolerance=±5% resistance=1k package=THT]
  J5 = male pin header, 3 pins [form="♂ (male)"]
  J4 = male pin header, 3 pins [form="♂ (male)"]
  J1 = male pin header, 3 pins [form="♂ (male)"]
  J2 = male pin header, 3 pins [form="♂ (male)"]
  J3 = male pin header, 3 pins [form="♂ (male)"]

nets:
  N1: Q1.E, J2.pin1, J2.pin2, J2.pin3
  N2: Q1.B, R1.Pin_1
  N3: Q1.C, J5.pin1, J4.pin1, J1.pin1
  N4: R1.Pin_0, J5.pin2, J4.pin2, J1.pin2
  N5: J5.pin3, J4.pin3, J1.pin3, J3.pin1, J3.pin2, J3.pin3
