# Fritzing sketch voltageDivider (saved by Fritzing 0.9.3b)
perfboards: 1

parts:
  R1 = Resistor [tolerance=±5% resistance=1k package=THT]
  R2 = Resistor [tolerance=±5% resistance=2k package=THT]
  J1 = female pin header, 2 pins [form="♀ (female)" part_number=Signal]
  J2 = female pin header, 2 pins [form="♀ (female)" part_number=GND]
  J3 = female pin header, 2 pins [form="♀ (female)" part_number="Signal divided"]

nets:
  N1: R1.Pin_0, R2.Pin_0, J3.pin1, J3.pin2
  N2: R1.Pin_1, J1.pin1, J1.pin2
  N3: R2.Pin_1, J2.pin1, J2.pin2
