# Fritzing sketch voltageRegulator (saved by Fritzing 0.9.3b)
circuit board: 2.8918cm x 1.1833cm
perfboards: 1

parts:
  IC1 = Voltage Regulator [package=78xxl]
  C1 = Ceramic Capacitor [capacitance=22µF voltage=50V part_number=0.33uF package="100 mil [THT, multilayer]"]
  C2 = Ceramic Capacitor [capacitance=0.1µF voltage=50V part_number=0.1uF package="100 mil [THT, multilayer]"]
  J1 = male pin header, 2 pins [form="♂ (male)"]
  J2 = male pin header, 2 pins [form="♂ (male)"]
  J3 = male pin header, 2 pins [form="♂ (male)"]
  J4 = male pin header, 2 pins [form="♂ (male)"]

nets:
  N1: IC1.GND, C1.0, C2.1, J2.pin1, J2.pin2, J4.pin1, J4.pin2
  N2: IC1.IN, C1.1, J1.pin1, J1.pin2
  N3: IC1.OUT, C2.0, J3.pin1, J3.pin2
